// Logisim project libreria_proyecto.circ as structural Verilog: 7 circuits, main circuit visualizador
module visualizador (
  input  Enable,
  input  D,
  input  C,
  input  B,
  input  A,
  output a_2,
  output b_2,
  output c_2,
  output d_2,
  output e,
  output f,
  output g
);

  wire and_1_out, and_2_out, and_3_out, and_4_out, and_5_out, and_6_out, and_7_out, and_8_out, and_11_out,
       and_12_out, not_1_out, not_2_out, not_3_out, not_4_out, not_5_out, not_6_out, not_7_out, not_8_out,
       not_9_out, not_10_out, not_11_out, not_12_out, not_13_out, not_14_out, not_15_out, not_16_out,
       not_17_out, not_18_out, not_19_out, not_20_out, not_21_out, not_22_out, not_23_out, not_24_out,
       not_25_out, not_26_out, not_27_out, not_28_out, not_29_out, not_30_out, not_31_out;

  not not_1 (not_1_out, D);
  not not_2 (not_2_out, C);
  not not_3 (not_3_out, A);
  not not_4 (not_4_out, D);
  not not_5 (not_5_out, C);
  not not_6 (not_6_out, D);
  not not_7 (not_7_out, C);
  not not_8 (not_8_out, D);
  not not_9 (not_9_out, B);
  not not_10 (not_10_out, A);
  not not_11 (not_11_out, D);
  not not_12 (not_12_out, B);
  not not_13 (not_13_out, A);
  not not_14 (not_14_out, D);
  not not_15 (not_15_out, C);
  not not_16 (not_16_out, D);
  not not_17 (not_17_out, C);
  not not_18 (not_18_out, A);
  not not_19 (not_19_out, D);
  not not_20 (not_20_out, C);
  not not_21 (not_21_out, D);
  not not_22 (not_22_out, C);
  not not_23 (not_23_out, A);
  not not_24 (not_24_out, D);
  not not_25 (not_25_out, B);
  not not_26 (not_26_out, A);
  not not_27 (not_27_out, D);
  not not_28 (not_28_out, C);
  not not_29 (not_29_out, D);
  not not_30 (not_30_out, B);
  not not_31 (not_31_out, A);
  and and_1 (and_1_out, Enable, not_1_out, not_2_out, not_3_out);
  and and_2 (and_2_out, Enable, not_4_out, not_5_out, B);
  and and_3 (and_3_out, Enable, not_6_out, not_7_out);
  and and_4 (and_4_out, Enable, not_8_out, not_9_out, not_10_out);
  and and_5 (and_5_out, Enable, not_11_out, not_12_out, not_13_out);
  and and_6 (and_6_out, Enable, not_14_out, not_15_out, A);
  and and_7 (and_7_out, Enable, not_16_out, not_17_out, not_18_out);
  and and_8 (and_8_out, Enable, not_19_out, not_20_out, B);
  and and_9 (e, Enable, not_21_out, not_22_out, not_23_out);
  and and_10 (f, Enable, not_24_out, not_25_out, not_26_out);
  and and_11 (and_11_out, Enable, not_27_out, not_28_out, B);
  and and_12 (and_12_out, Enable, not_29_out, C, not_30_out, not_31_out);
  or or_1 (a_2, and_1_out, and_2_out);
  or or_2 (b_2, and_3_out, and_4_out);
  or or_3 (c_2, and_5_out, and_6_out);
  or or_4 (d_2, and_7_out, and_8_out);
  or or_5 (g, and_11_out, and_12_out);

  // Notes on the sheet:
  //   Recibe cuatro bits como entrada e ilumina el display de 0 a 4
endmodule

module memBoton (
  input  B,
  input  R_asincrono,
  input  CLK,
  input  E,
  input  R_sincrono,
  output S
);

  S_R_Flip_Flop s_r_ff_1 (.S(B), .clk(CLK), .R(R_sincrono), .Q(S), .reset(R_asincrono), .en(E));  // open: Qn, preset

  // Notes on the sheet:
  //   Si se pulsa B, se guarda un uno hasta que se pulse R. Solo funcionan si E está pulsado.
  //   El reset síncrono se activará cuando se pulse otro botón de piso, y el asíncrono cuando se pulse el de reset
endmodule

module contador3Bits (
  input  E,
  input  CLK,
  input  RMan,
  input  LimB2,
  input  LimB1,
  input  LimB0,
  output FinCiclo
);

  wire j_k_ff_1_qn, j_k_ff_2_qn, or_1_out;
  wire [2:0] j_k_ff_1_q;

  J_K_Flip_Flop j_k_ff_1 (
    .J(E), .clk(CLK), .K(E), .Q(j_k_ff_1_q[0]), .Qn(j_k_ff_1_qn), .en(E), .reset(or_1_out));  // open: preset
  or or_1 (or_1_out, RMan, FinCiclo);
  J_K_Flip_Flop j_k_ff_2 (
    .J(E), .clk(j_k_ff_1_qn), .K(E), .Q(j_k_ff_1_q[1]), .Qn(j_k_ff_2_qn), .en(E), .reset(or_1_out));  // open: preset
  J_K_Flip_Flop j_k_ff_3 (
    .J(E), .clk(j_k_ff_2_qn), .K(E), .Q(j_k_ff_1_q[2]), .en(E), .reset(or_1_out));  // open: Qn, preset
  Comparator #(.width(3), .mode("unsigned")) comparator_1 (
    .a(j_k_ff_1_q), .b({LimB2, LimB1, LimB0}), .eq(FinCiclo));  // open: gt, lt

  // Notes on the sheet:
  //   Si está pulsado el enable, cuenta hasta que se pulse el reset o el número contado sea igual al límite
endmodule

module incrementoDecremento (
  input  NB2,
  input  NB1,
  input  NB0,
  input  _1B2,
  input  _1B1,
  input  _1B0,
  output plus_B2,
  output plus_B1,
  output plus_B0,
  output minus_B2,
  output minus_B1,
  output minus_B0
);

  Adder #(.width(3)) adder_1 (
    .a({NB2, NB1, NB0}), .b({_1B2, _1B1, _1B0}), .out({plus_B2, plus_B1, plus_B0}));  // open: cin, cout
  Subtractor #(.width(3)) subtractor_1 (
    .a({NB2, NB1, NB0}), .b({_1B2, _1B1, _1B0}), .out({minus_B2, minus_B1, minus_B0}));  // open: bin, bout

  // Notes on the sheet:
  //   Los 3 bits del numero al que vamos a sumar/restar 1
  //   Los 3 bits del numero que le vamos a restar, que por defecto va a ser 1
  //   Los 3 bits de la suma
  //   Los 3 bits de la resta
endmodule

module registro3Bits (
  input  D2,
  input  D1,
  input  D0,
  input  R,
  input  CLK,
  input  E,
  output PTB2,
  output PTB1,
  output PTB0
);

  wire not_1_out, not_2_out, not_3_out;

  not not_1 (not_1_out, D2);
  not not_2 (not_2_out, D1);
  S_R_Flip_Flop s_r_ff_1 (.S(D2), .clk(CLK), .R(not_1_out), .Q(PTB2), .preset(R), .reset(R), .en(E));  // open: Qn
  not not_3 (not_3_out, D0);
  S_R_Flip_Flop s_r_ff_2 (.S(D1), .clk(CLK), .R(not_2_out), .Q(PTB1), .preset(R), .reset(R), .en(E));  // open: Qn
  S_R_Flip_Flop s_r_ff_3 (.S(D0), .clk(CLK), .R(not_3_out), .Q(PTB0), .preset(R), .reset(R), .en(E));  // open: Qn

  // Notes on the sheet:
  //   Funciona de forma parecida al memBoton pero con 3 bits. Guarda los valores de los 3 bits introducidos
endmodule

module selector (
  input  subo,
  input  bajo,
  input  bitSubo,
  input  bitBajo,
  output Salida
);

  wire and_1_out, and_2_out;

  and and_1 (and_1_out, subo, bitSubo);
  and and_2 (and_2_out, bajo, bitBajo);
  or or_1 (Salida, and_1_out, and_2_out);

  // Notes on the sheet:
  //   Si sube, devuelve bitSubo
  //   Si baja, devuelve bitBajo
endmodule

module codificadorBoton (
  input  PB,
  input  P1,
  input  P2,
  input  P3,
  input  P4,
  output B2,
  output B1,
  output B0
);

  wire and_2_out, and_3_out, and_4_out, and_5_out, not_1_out, not_2_out, not_3_out, not_4_out, not_5_out,
       not_6_out, not_7_out, not_8_out, not_9_out, not_10_out, not_11_out, not_12_out, not_13_out,
       not_14_out, not_15_out, not_16_out, not_17_out, not_18_out, not_19_out, not_20_out;

  not not_1 (not_1_out, PB);
  not not_2 (not_2_out, P1);
  not not_3 (not_3_out, P2);
  not not_4 (not_4_out, P3);
  not not_5 (not_5_out, PB);
  not not_6 (not_6_out, P1);
  not not_7 (not_7_out, P2);
  not not_8 (not_8_out, P4);
  not not_9 (not_9_out, PB);
  not not_10 (not_10_out, P1);
  not not_11 (not_11_out, P3);
  not not_12 (not_12_out, P4);
  not not_13 (not_13_out, PB);
  not not_14 (not_14_out, P1);
  not not_15 (not_15_out, P2);
  not not_16 (not_16_out, P4);
  not not_17 (not_17_out, PB);
  not not_18 (not_18_out, P2);
  not not_19 (not_19_out, P3);
  not not_20 (not_20_out, P4);
  and and_1 (B2, not_1_out, not_2_out, not_3_out, not_4_out, P4);
  and and_2 (and_2_out, not_5_out, not_6_out, not_7_out, P3, not_8_out);
  and and_3 (and_3_out, not_9_out, not_10_out, P2, not_11_out, not_12_out);
  and and_4 (and_4_out, not_13_out, not_14_out, not_15_out, P3, not_16_out);
  and and_5 (and_5_out, not_17_out, P1, not_18_out, not_19_out, not_20_out);
  or or_1 (B1, and_2_out, and_3_out);
  or or_2 (B0, and_4_out, and_5_out);

  // Notes on the sheet:
  //   Dependiendo del botón que se pulse devuelve un valor u otro. Si no se pulsa nada o se pulsan varios a la vez, devuelve 0
endmodule
