// Logisim project proyecto_definitivo.circ as structural Verilog: 1 circuit, main circuit main
module main (
  input  _0,
  input  ENABLE,
  input  in_3,
  input  in_4,
  input  in_5,
  input  in_6,
  input  \_4__límite ,
  input  in_8
);

  wire CLK_out, comparator_1_eq, comparator_1_gt, comparator_1_lt, contador3bits_1_finciclo,
       incrementodecremento_1_minus_b0, incrementodecremento_1_minus_b1, incrementodecremento_1_minus_b2,
       incrementodecremento_1_plus_b0, incrementodecremento_1_plus_b1, incrementodecremento_1_plus_b2,
       memboton_1_s, memboton_2_s, memboton_3_s, memboton_4_s, memboton_5_s, not_1_out, or_1_out, or_2_out,
       or_3_out, or_4_out, or_5_out, P1_out, P2_out, P3_out, P4_out, PB_out, RESET_out, selector_1_salida,
       selector_2_salida, selector_3_salida, visualizador_1_a_2, visualizador_1_b_2, visualizador_1_c_2,
       visualizador_1_d_2, visualizador_1_e, visualizador_1_f, visualizador_1_g;
  wire [2:0] codificadorboton_1_b0, registro3bits_1_ptb0;

  Button RESET (.out(RESET_out));
  Button PB (.out(PB_out));
  Clock CLK (.out(CLK_out));
  Button P1 (.out(P1_out));
  Button P3 (.out(P3_out));
  Button P2 (.out(P2_out));
  Button P4 (.out(P4_out));
  or or_1 (or_1_out, P1_out, P2_out, P3_out, P4_out);
  or or_2 (or_2_out, PB_out, P2_out, P3_out, P4_out);
  or or_3 (or_3_out, PB_out, P1_out, P3_out, P4_out);
  or or_4 (or_4_out, PB_out, P1_out, P2_out, P4_out);
  or or_5 (or_5_out, PB_out, P1_out, P2_out, P3_out);
  memBoton memboton_1 (
    .B(PB_out), .R_asincrono(RESET_out), .CLK(CLK_out), .E(ENABLE), .R_sincrono(or_1_out), .S(memboton_1_s));
  memBoton memboton_2 (
    .B(P1_out), .R_asincrono(RESET_out), .CLK(CLK_out), .E(ENABLE), .R_sincrono(or_2_out), .S(memboton_2_s));
  memBoton memboton_3 (
    .B(P2_out), .R_asincrono(RESET_out), .CLK(CLK_out), .E(ENABLE), .R_sincrono(or_3_out), .S(memboton_3_s));
  memBoton memboton_4 (
    .B(P3_out), .R_asincrono(RESET_out), .CLK(CLK_out), .E(ENABLE), .R_sincrono(or_4_out), .S(memboton_4_s));
  memBoton memboton_5 (
    .B(P4_out), .R_asincrono(RESET_out), .CLK(CLK_out), .E(ENABLE), .R_sincrono(or_5_out), .S(memboton_5_s));
  codificadorBoton codificadorboton_1 (
    .PB(memboton_1_s), .P1(memboton_2_s), .P2(memboton_3_s), .P3(memboton_4_s), .P4(memboton_5_s),
    .B2(codificadorboton_1_b0[2]), .B1(codificadorboton_1_b0[1]), .B0(codificadorboton_1_b0[0]));
  contador3Bits contador3bits_1 (
    .E(ENABLE), .CLK(CLK_out), .RMan(RESET_out), .LimB2(in_6), .LimB1(\_4__límite ), .LimB0(in_8),
    .FinCiclo(contador3bits_1_finciclo));
  incrementoDecremento incrementodecremento_1 (
    .NB2(registro3bits_1_ptb0[2]), .NB1(registro3bits_1_ptb0[1]), .NB0(registro3bits_1_ptb0[0]), ._1B2(in_3),
    ._1B1(in_4), ._1B0(in_5), .plus_B2(incrementodecremento_1_plus_b2),
    .plus_B1(incrementodecremento_1_plus_b1), .plus_B0(incrementodecremento_1_plus_b0),
    .minus_B2(incrementodecremento_1_minus_b2), .minus_B1(incrementodecremento_1_minus_b1),
    .minus_B0(incrementodecremento_1_minus_b0));
  Comparator #(.width(3), .mode("unsigned")) comparator_1 (
    .a(codificadorboton_1_b0), .b(registro3bits_1_ptb0), .gt(comparator_1_gt), .eq(comparator_1_eq),
    .lt(comparator_1_lt));
  selector selector_1 (
    .subo(comparator_1_gt), .bajo(comparator_1_lt), .bitSubo(incrementodecremento_1_plus_b2),
    .bitBajo(incrementodecremento_1_minus_b2), .Salida(selector_1_salida));
  selector selector_2 (
    .subo(comparator_1_gt), .bajo(comparator_1_lt), .bitSubo(incrementodecremento_1_plus_b1),
    .bitBajo(incrementodecremento_1_minus_b1), .Salida(selector_2_salida));
  selector selector_3 (
    .subo(comparator_1_gt), .bajo(comparator_1_lt), .bitSubo(incrementodecremento_1_plus_b0),
    .bitBajo(incrementodecremento_1_minus_b0), .Salida(selector_3_salida));
  not not_1 (not_1_out, comparator_1_eq);
  registro3Bits registro3bits_1 (
    .D2(selector_1_salida), .D1(selector_2_salida), .D0(selector_3_salida), .R(RESET_out),
    .CLK(contador3bits_1_finciclo), .E(not_1_out), .PTB2(registro3bits_1_ptb0[2]),
    .PTB1(registro3bits_1_ptb0[1]), .PTB0(registro3bits_1_ptb0[0]));
  visualizador visualizador_1 (
    .Enable(ENABLE), .D(_0), .C(registro3bits_1_ptb0[2]), .B(registro3bits_1_ptb0[1]),
    .A(registro3bits_1_ptb0[0]), .a_2(visualizador_1_a_2), .b_2(visualizador_1_b_2),
    .c_2(visualizador_1_c_2), .d_2(visualizador_1_d_2), .e(visualizador_1_e), .f(visualizador_1_f),
    .g(visualizador_1_g));
  _7_Segment_Display u_7_segment_display_1 (
    .g(visualizador_1_g), .f(visualizador_1_f), .a(visualizador_1_a_2), .b(visualizador_1_b_2),
    .e(visualizador_1_e), .d(visualizador_1_d_2), .c(visualizador_1_c_2));  // open: dp

  // Notes on the sheet:
  //   Número del botón que se pulsa
  //   El registro se actualiza cada vez que termina el ciclo del contador
  //   1 (el número sumado/restado a la planta actual)
  //   El registro se actualiza cuando el piso en el que estamos y al que queremos ir no son iguales
  //   Número que hay en el registro
endmodule
